# Fritzing sketch arduinothing (saved by Fritzing 0.9.0b)
breadboards: 1

parts:
  Part1 = Arduino Uno (Rev3) - ICSP
  R1 = Photocell (LDR) [package=THT]  # not connected
  R2 = Resistor [package="2512 [SMD]"]

nets:
  N1: Part1.A0, R2.Pin_0
  N2: Part1.GND, R2.Pin_1
